// Logisim project x3f7.circ as structural Verilog: 1 circuit, main circuit main
module main (
  input  X1,
  input  X2,
  input  X3,
  input  in_4,
  output F1,
  output F3,
  output F4,
  output F5,
  output F6,
  output F2,
  output F7
);

  wire and_1_out, and_2_out, and_3_out, not_1_out, not_2_out, or_1_out, xor_1_out;

  not not_1 (not_1_out, X1);
  not not_2 (not_2_out, X2);
  and and_1 (and_1_out, not_2_out, X1);
  xor xor_1 (xor_1_out, X1, X3);
  or or_1 (or_1_out, not_2_out, X3);
  and and_2 (and_2_out, not_1_out, X2);
  and and_3 (and_3_out, X2, xor_1_out);
  and and_4 (F1, X1, X2);
  and and_5 (F3, or_1_out, X1);
  or or_2 (F4, not_2_out, and_2_out);
  or or_3 (F5, and_1_out, and_3_out);

  assign F2 = in_4;
  assign F6 = X2;
  assign F7 = in_4;
endmodule
